# Fritzing sketch LED_sensor (saved by Fritzing 0.8.5b)
circuit board: 16.9333cm x 5.64444cm
breadboards: 1

parts:
  LED1 = LED - 5mm [color="White (6500K)" package="5 mm [THT]"]
  R2 = Photocell (LDR) [package=THT]
  R3 = Resistor [tolerance=±5% resistance=330 package=THT]
  Part1 = Arduino Uno (Rev3)
  R1 = Resistor [tolerance=±5% resistance=220 package=THT]

nets:
  N1: LED1.cathode, LED1.anode, Part1.D11_PWM/MOSI, R1.Pin_0
  N2: R2.pin_0, Part1.5V
  N3: R2.pin_1, R3.Pin_1, Part1.A0
  N4: R3.Pin_0, Part1.GND, R1.Pin_1
